// Logisim project ICTester.circ as structural Verilog: 10 circuits, main circuit main
module main (
  input  Enable,
  output out_2,
  output Found,
  output NotFound,
  output C0,
  output C1
);

  wire _2_Bit_Count_l0, _2_Bit_Count_l1, _4Bit_Counter_l2, _4Bit_Counter_l3, clock_1_out,
       Ctrl_2Bit_Count_counter_enable, Ctrl_2Bit_Count_counter_reset, ctrl_4bit_count_1__4bit_count__enable,
       ctrl_4bit_count_1_reset_2, Matching_4Xnor_3And_f, not_1_out, Reset_out, undriven, undriven_2,
       undriven_3, undriven_4, undriven_5, undriven_6, undriven_7, undriven_8, undriven_9, undriven_10,
       undriven_11, undriven_12, undriven_13, undriven_14, undriven_15, undriven_16;

  Button Reset (.out(Reset_out));
  Ctrl_4Bit_Count ctrl_4bit_count_1 (
    .ENABLE(Enable), .Found(Found), .NotFound(NotFound), .RESET(Reset_out),
    ._4Bit_Count__Enable(ctrl_4bit_count_1__4bit_count__enable), .Reset_2(ctrl_4bit_count_1_reset_2));
  Clock clock_1 (.out(clock_1_out));
  _4_Bit_Counter _4Bit_Counter (
    .Enable(ctrl_4bit_count_1__4bit_count__enable), .CLK(clock_1_out), .L0(C0), .L1(C1),
    .L2(_4Bit_Counter_l2), .L3(_4Bit_Counter_l3), .Clear(ctrl_4bit_count_1_reset_2));
  GenerateRightOutput_And_Or_Xor_Nand_Multiplexer GenerateOutput (
    .a(_4Bit_Counter_l3), .b(_4Bit_Counter_l2), .c(C1), .d(C0), .out_5(out_2));
  Matching_4Xnor_3And Matching_4Xnor_3And (
    .test(out_2), .g0(undriven), .g1(undriven_2), .g2(undriven_3), .g3(undriven_4), .f(Matching_4Xnor_3And_f));
  Ctrl_2Bit_Count Ctrl_2Bit_Count (
    .MatchingCirc(Matching_4Xnor_3And_f), .Counter_Enable(Ctrl_2Bit_Count_counter_enable),
    .Reset_a__L3_4Bit_count(_4Bit_Counter_l3), .Counter_Reset(Ctrl_2Bit_Count_counter_reset),
    .Reset_b__L2_4Bit_count(_4Bit_Counter_l2), .Enable(Enable), .Found(Found), .NotFound(NotFound),
    .ClkOf_Counter1(clock_1_out));
  not not_1 (not_1_out, clock_1_out);
  _2_Bit_Counter _2_Bit_Count (
    .Enable(Ctrl_2Bit_Count_counter_enable), .CLK(not_1_out), .L0(_2_Bit_Count_l0), .L1(_2_Bit_Count_l1),
    .Clear(Ctrl_2Bit_Count_counter_reset));
  DetectionCirc_Notfound_Or_found DetectionCirc (
    .L0_Of_2222_Bit__counter(_2_Bit_Count_l0), .L1_Of_2222_Bit__counter(_2_Bit_Count_l1),
    ._4th_Match(Matching_4Xnor_3And_f), .L3_Of_4444_Bit__counter(_4Bit_Counter_l3),
    .L2_Of_4444_Bit__counter(_4Bit_Counter_l2), .L1_Of_4444_Bit__counter(C1), .L0_Of_4444_Bit__counter(C0),
    .Counter_1_CLK(clock_1_out), .RESET(Reset_out), .Found(Found), .NotFound(NotFound));
  // AND_Gate and_1 has open pins: in0=undriven_5, in1=undriven_8, out=open
  // AND_Gate and_2 has open pins: in0=undriven_5, in1=undriven_8, out=open
  // AND_Gate and_3 has open pins: in0=undriven_5, in1=undriven_8, out=open
  // AND_Gate and_4 has open pins: in0=undriven_5, in1=undriven_8, out=open
  // NAND_Gate nand_1 has open pins: in0=undriven_6, in1=undriven_9, out=open
  // NAND_Gate nand_2 has open pins: in0=undriven_6, in1=undriven_9, out=open
  // NAND_Gate nand_3 has open pins: in0=undriven_6, in1=undriven_9, out=open
  // NAND_Gate nand_4 has open pins: in0=undriven_6, in1=undriven_9, out=open
  // NOR_Gate nor_1 has open pins: in0=undriven_7, in1=undriven_10, out=open
  // NOR_Gate nor_2 has open pins: in0=undriven_7, in1=undriven_10, out=open
  // NOR_Gate nor_3 has open pins: in0=undriven_7, in1=undriven_10, out=open
  // NOR_Gate nor_4 has open pins: in0=undriven_7, in1=undriven_10, out=open
  // XOR_Gate xor_1 has open pins: in0=undriven_12, in1=undriven_15, out=open
  // XOR_Gate xor_2 has open pins: in0=undriven_12, in1=undriven_15, out=open
  // XOR_Gate xor_3 has open pins: in0=undriven_12, in1=undriven_15, out=open
  // XOR_Gate xor_4 has open pins: in0=undriven_12, in1=undriven_15, out=open
  // OR_Gate or_1 has open pins: in0=undriven_14, in1=undriven_16, out=open
  // OR_Gate or_2 has open pins: in0=undriven_14, in1=undriven_16, out=open
  // OR_Gate or_3 has open pins: in0=undriven_14, in1=undriven_16, out=open
  // OR_Gate or_4 has open pins: in0=undriven_14, in1=undriven_16, out=open
  // NOR_Gate nor_5 has open pins: in0=undriven_11, in1=undriven_13, out=open
  // NAND_Gate nand_5 has open pins: in0=undriven_11, in1=undriven_13, out=open
  // NOR_Gate nor_6 has open pins: in0=undriven_11, in1=undriven_13, out=open
  // NOR_Gate nor_7 has open pins: in0=undriven_11, in1=undriven_13, out=open
endmodule

module Matching_4Xnor_3And (
  input  test,
  input  g0,
  input  g1,
  input  g2,
  input  g3,
  output f
);

  wire and_1_out, and_2_out, xnor_1_out, xnor_2_out, xnor_3_out, xnor_4_out;

  xnor xnor_1 (xnor_1_out, test, g0);
  xnor xnor_2 (xnor_2_out, test, g1);
  xnor xnor_3 (xnor_3_out, test, g2);
  xnor xnor_4 (xnor_4_out, test, g3);
  and and_1 (and_1_out, xnor_1_out, xnor_2_out);
  and and_2 (and_2_out, xnor_3_out, xnor_4_out);
  and and_3 (f, and_1_out, and_2_out);
endmodule

module GenerateRightOutput_And_Or_Xor_Nand_Multiplexer (
  input  a,
  input  b,
  input  c,
  input  d,
  output out_5
);

  wire and_1_out, nand_1_out, or_1_out, xor_1_out;

  and and_1 (and_1_out, a, b);
  or or_1 (or_1_out, a, b);
  xor xor_1 (xor_1_out, a, b);
  nand nand_1 (nand_1_out, a, b);
  Multiplexer #(.select(2), .enable("false")) multiplexer_1 (
    .in0(and_1_out), .in1(or_1_out), .in2(xor_1_out), .in3(nand_1_out), .out(out_5), .sel({d, c}));
endmodule

module _4_Bit_Counter (
  input  Enable,
  input  Clear,
  input  CLK,
  output L0,
  output L1,
  output L2,
  output L3
);

  wire halfadder_1_carry, halfadder_1_sum, halfadder_2_carry, halfadder_2_sum, halfadder_3_carry,
       halfadder_3_sum, halfadder_4_sum;

  HalfAdder halfadder_1 (.A(Enable), .B(L3), .Sum(halfadder_1_sum), .Carry(halfadder_1_carry));
  HalfAdder halfadder_2 (.A(L2), .B(halfadder_1_carry), .Sum(halfadder_2_sum), .Carry(halfadder_2_carry));
  HalfAdder halfadder_3 (.A(L1), .B(halfadder_2_carry), .Sum(halfadder_3_sum), .Carry(halfadder_3_carry));
  HalfAdder halfadder_4 (.A(L0), .B(halfadder_3_carry), .Sum(halfadder_4_sum));  // open: Carry
  D_Flip_Flop d_ff_1 (.clk(CLK), .D(halfadder_1_sum), .Q(L3), .en(1'b1), .reset(Clear));  // open: Qn, preset
  D_Flip_Flop d_ff_2 (.clk(CLK), .D(halfadder_2_sum), .Q(L2), .en(1'b1), .reset(Clear));  // open: Qn, preset
  D_Flip_Flop d_ff_3 (.clk(CLK), .D(halfadder_3_sum), .Q(L1), .en(1'b1), .reset(Clear));  // open: Qn, preset
  D_Flip_Flop d_ff_4 (.clk(CLK), .D(halfadder_4_sum), .Q(L0), .en(1'b1), .reset(Clear));  // open: Qn, preset
endmodule

module HalfAdder (
  input  A,
  input  B,
  output Sum,
  output Carry
);

  xor xor_1 (Sum, A, B);
  and and_1 (Carry, A, B);
endmodule

module _2_Bit_Counter (
  input  Enable,
  input  CLK,
  input  Clear,
  output L0,
  output L1
);

  wire halfadder_1_carry, halfadder_1_sum, halfadder_2_sum;

  HalfAdder halfadder_1 (.A(Enable), .B(L1), .Sum(halfadder_1_sum), .Carry(halfadder_1_carry));
  HalfAdder halfadder_2 (.A(L0), .B(halfadder_1_carry), .Sum(halfadder_2_sum));  // open: Carry
  D_Flip_Flop d_ff_1 (.clk(CLK), .D(halfadder_1_sum), .Q(L1), .en(1'b1), .reset(Clear));  // open: Qn, preset
  D_Flip_Flop d_ff_2 (.clk(CLK), .D(halfadder_2_sum), .Q(L0), .en(1'b1), .reset(Clear));  // open: Qn, preset
endmodule

module Ctrl_2Bit_Count (
  input  Reset_a__L3_4Bit_count,
  input  Reset_b__L2_4Bit_count,
  input  Enable,
  input  Found,
  input  NotFound,
  input  MatchingCirc,
  input  ClkOf_Counter1,
  output Counter_Reset,
  output Counter_Enable
);

  wire commonctrlcirc_enable_count_1_2_1_enable_counter_1_2, d_ff_1_q, not_1_out, not_2_out;

  not not_1 (not_1_out, Reset_a__L3_4Bit_count);
  and and_1 (Counter_Reset, not_1_out, not_2_out);
  not not_2 (not_2_out, Reset_b__L2_4Bit_count);
  CommonCtrlCirc_Enable__count_1_2 commonctrlcirc_enable_count_1_2_1 (
    .ENABLE(Enable), .Found(Found), .NotFound(NotFound),
    .Enable_counter_1_2(commonctrlcirc_enable_count_1_2_1_enable_counter_1_2));
  D_Flip_Flop d_ff_1 (
    .clk(ClkOf_Counter1), .D(MatchingCirc), .Q(d_ff_1_q), .preset(1'b0), .en(1'b1), .reset(1'b0));  // open: Qn
  and and_2 (Counter_Enable, commonctrlcirc_enable_count_1_2_1_enable_counter_1_2, d_ff_1_q);
endmodule

module CommonCtrlCirc_Enable__count_1_2 (
  input  ENABLE,
  input  Found,
  input  NotFound,
  output Enable_counter_1_2
);

  wire not_1_out, or_1_out;

  or or_1 (or_1_out, Found, NotFound);
  not not_1 (not_1_out, or_1_out);
  and and_1 (Enable_counter_1_2, ENABLE, not_1_out);

  // Notes on the sheet:
  //   This Circit always returns 1 and returns 0 if found high or not found high
endmodule

module DetectionCirc_Notfound_Or_found (
  input  L0_Of_2222_Bit__counter,
  input  L1_Of_2222_Bit__counter,
  input  _4th_Match,
  input  L3_Of_4444_Bit__counter,
  input  L2_Of_4444_Bit__counter,
  input  L1_Of_4444_Bit__counter,
  input  L0_Of_4444_Bit__counter,
  input  Counter_1_CLK,
  input  RESET,
  output Found,
  output NotFound
);

  wire and_1_out, and_2_out, and_3_out, and_5_out, and_6_out, not_1_out, or_1_out;

  and and_1 (and_1_out, L0_Of_2222_Bit__counter, L1_Of_2222_Bit__counter);
  and and_2 (and_2_out, L3_Of_4444_Bit__counter, L2_Of_4444_Bit__counter);
  and and_3 (and_3_out, L1_Of_4444_Bit__counter, L0_Of_4444_Bit__counter);
  and and_4 (Found, and_1_out, _4th_Match);
  not not_1 (not_1_out, Found);
  and and_5 (and_5_out, and_2_out, and_3_out);
  and and_6 (and_6_out, not_1_out, and_5_out);
  or or_1 (or_1_out, NotFound, and_6_out);
  D_Flip_Flop d_ff_1 (.clk(Counter_1_CLK), .D(or_1_out), .Q(NotFound), .en(1'b1), .reset(RESET));  // open: Qn, preset
endmodule

module Ctrl_4Bit_Count (
  input  ENABLE,
  input  Found,
  input  NotFound,
  input  RESET,
  output _4Bit_Count__Enable,
  output Reset_2
);

  CommonCtrlCirc_Enable__count_1_2 CommonCtrlCirc_Enable (
    .ENABLE(ENABLE), .Found(Found), .NotFound(NotFound), .Enable_counter_1_2(_4Bit_Count__Enable));

  assign Reset_2 = RESET;
endmodule
